# Fritzing sketch AxRobot (saved by Fritzing 0.9.9b)

parts:
  Mod1 = Arduino Sensor Shield v5.0
  S1 = H-Bridge with L298N
  HC-SR04_Sensor_1 = HC-SR04 Ultrasonic Distance Sensor
  M1 = DC Motor
  M2 = DC Motor
  Mod2 = KY-022 Infrared Receiver Module [package="Breakout board"]
  o1 = Module display OLED I2C 128x64 SSD1306 [package=THT]
  Part1 = KY-033 Tracing Black White Line Hunting Sensor Module For Arduino
  Part2 = KY-033 Tracing Black White Line Hunting Sensor Module For Arduino
  Part3 = KY-033 Tracing Black White Line Hunting Sensor Module For Arduino
  Part4 = Bluetooth HM-10
  R1 = Resistor [tolerance=±5% resistance=1k package="1206 [SMD]"]
  VCC1 = Battery
  J1 = Basic Servo  # not connected

nets:
  N1: Mod1.VCC, Mod1.AREF-V, Mod1.4-V, Mod1.3-V, Mod1.2-V, S1.ENA-5V, Part1.V+, Part2.V+, Part3.V+
  N2: Mod1.SD-D11, Mod1.11-S, Part4.TXD, Part4.GND
  N3: Mod1.SD-D13, Mod1.13-S, HC-SR04_Sensor_1.TRIG
  N4: Mod1.SD-D12, Mod1.12-S, HC-SR04_Sensor_1.ECHO
  N5: Mod1.URF01-A0, Mod1.A0-SIG, Mod2.Vin, Mod2.S
  GND: Mod1.GND, Mod1.4-G, Mod1.3-G, Mod1.2-G, Part1.GND, Part2.GND, Part3.GND
  N6: Mod1.A2-SIG, S1.IN4
  N7: Mod1.A3-SIG, R1.Pin_0
  N8: Mod1.A4-SIG, o1.SDA
  N9: Mod1.A5-SIG, o1.SCL
  N10: Mod1.10-S, Mod1.ParallelLCD-D10, S1.IN3
  N11: Mod1.9-S, Mod1.ParallelLCD-D9, S1.IN2
  N12: Mod1.8-S, Mod1.ParallelLCD-D8, S1.IN1
  N13: Mod1.6-S, Mod1.ParallelLCD-D6, S1.ENB
  N14: Mod1.5-S, Mod1.ParallelLCD-D5, S1.ENA
  N15: Mod1.4-S, Mod1.SerialLCD-D4, Part2.S
  N16: Mod1.3-S, Mod1.ParallelLCD-D3, Part3.S
  N17: Mod1.2-S, Mod1.SerialLCD-D2, Part1.S
  N18: S1.12V, VCC1.+
  N19: S1.GND, VCC1.-
  N20: S1.M1-01, M2.pin_2
  N21: S1.M1-02, M2.pin_1
  N22: S1.M2-01, M1.pin_2
  N23: S1.M2-02, M1.pin_1
  N24: Part4.RXD, R1.Pin_1

notes:
  Please tie all unwired black wires to "G" (GND) and all unwired red wires to "V" (VCC)

custom parts:
  H-Bridge with L298N: h-bridge
  KY-022 Infrared Receiver Module: KY-022 IR receiver module, reacts to 38kHz infrared light.
  Module display OLED I2C 128x64 SSD1306: Ecran OLED I2C SSD163 de 128x64 avec connexion I2C
  KY-033 Tracing Black White Line Hunting Sensor Module For Arduino: Tracing Black White Line Hunting Sensor Module For Arduino Description: This is KY-033 tracking sensor. The KY-033 measures the intensity of infrared radiation and delivers it as an analog output voltage. Features: Operating voltage: 2.5 - 12V(cannot over12V) working current: 18mA-20mA at 5V Enhanced accuracy Documents: http://www.vishay.com/docs/83760/tcrt5000.pdf
  Battery: Your standard 2x 18650 battery pack (7,4 Volts)
